# Fritzing sketch E.fzzSP8266+DHT22+PIR+Led (saved by Fritzing 0.9.9b)

parts:
  U1 = ESP8266 NodeMCU LoLin module
  DHT1 = DHT22 Humidity and Temperature Sensor
  R1 = Resistor [tolerance=±5% resistance=220 package="2512 [SMD]"]
  PIR1 = PIR sensor
  LED1 = LED - 5mm [color="Red (633nm)" current=0.030 package="5 mm [THT]"]
  R2 = Resistor [tolerance=±5% resistance=220 package="2512 [SMD]"]
  LED2 = LED - 5mm [color="Blue (505nm)" current=0.030 package="5 mm [THT]"]
  R3 = Resistor [tolerance=±5% resistance=220 package="2512 [SMD]"]

nets:
  N1: U1.D1, R2.Pin_1
  N2: U1.D2, DHT1.DATA, R1.Pin_1
  N3: U1.D3, R3.Pin_1
  VDD: U1.3V3, DHT1.VDD, R1.Pin_0, PIR1.VDD
  GND: U1.GND, DHT1.GND, PIR1.GND, LED1.anode, LED2.anode
  N4: LED1.cathode, R2.Pin_0
  N5: LED2.cathode, R3.Pin_0

custom parts:
  ESP8266 NodeMCU LoLin module: ESP8266 based NodeMCU
